// Logisim project ROMANELLI.circ as structural Verilog: 5 circuits, main circuit main
module main (
);

  // DisplayDecoder displaydecoder_1: pin names not known
  _7_Segment_Display u_7_segment_display_1 ();  // open: g, f, a, b, e, d, c, dp
endmodule

module meio_somador (
  input  in_1,
  input  in_2,
  output out_3,
  output out_4
);

  and and_1 (out_4, in_1, in_1);
  xor xor_1 (out_3, in_1, in_2);
endmodule

module somador_completo (
  input  in_1,
  input  in_2,
  input  in_3,
  output out_4,
  output out_5
);

  wire meio_somador_1_out_3, meio_somador_1_out_4, meio_somador_2_out_4;

  meio_somador meio_somador_1 (.in_1(in_2), .in_2(in_3), .out_4(meio_somador_1_out_4), .out_3(meio_somador_1_out_3));
  meio_somador meio_somador_2 (.in_1(in_1), .in_2(meio_somador_1_out_3), .out_4(meio_somador_2_out_4), .out_3(out_4));
  or or_1 (out_5, meio_somador_1_out_4, meio_somador_2_out_4);
endmodule

module somador_de_4_bits (
  input  in_1,
  input  in_2,
  input  in_3,
  input  in_4,
  input  in_5,
  input  in_6,
  input  in_7,
  input  in_8,
  input  in_9,
  input  in_10,
  output out_11,
  output out_12,
  output out_13,
  output out_14
);

  wire somador_completo_1_out_5, somador_completo_2_out_5, somador_completo_4_out_5;

  somador_completo somador_completo_1 (
    .in_2(in_4), .in_3(in_5), .in_1(somador_completo_4_out_5), .out_5(somador_completo_1_out_5),
    .out_4(out_12));
  somador_completo somador_completo_2 (
    .in_2(in_6), .in_3(in_7), .in_1(somador_completo_1_out_5), .out_5(somador_completo_2_out_5),
    .out_4(out_13));
  somador_completo somador_completo_3 (
    .in_2(in_8), .in_3(in_9), .in_1(somador_completo_2_out_5), .out_5(in_10), .out_4(out_14));
  somador_completo somador_completo_4 (
    .in_2(in_2), .in_3(in_3), .in_1(in_1), .out_5(somador_completo_4_out_5), .out_4(out_11));
endmodule

module decodificador (
  input  E3,
  input  E2,
  input  E1,
  input  E0,
  output A,
  output B,
  output C,
  output D,
  output E,
  output F,
  output G
);

  wire and_1_out, and_2_out, and_3_out, and_4_out, and_5_out, and_6_out, and_7_out, and_8_out, and_9_out,
       and_10_out, and_11_out, and_12_out, and_13_out, and_14_out, and_15_out, and_16_out, and_17_out,
       and_18_out, and_19_out, and_20_out, and_21_out, and_22_out, and_23_out, and_24_out, and_25_out,
       and_26_out, and_27_out, and_28_out, and_29_out, not_1_out, not_2_out, not_3_out, not_4_out, not_5_out,
       not_6_out, not_7_out, not_8_out, not_9_out, not_10_out, not_11_out, not_12_out, not_13_out,
       not_14_out, not_15_out, not_16_out, not_17_out, not_18_out, not_19_out, not_20_out, not_21_out,
       not_22_out, not_23_out, not_24_out, not_25_out, not_26_out, not_27_out, not_28_out, not_29_out,
       not_30_out, not_31_out, not_32_out, not_33_out, not_34_out, not_35_out, not_36_out, not_37_out,
       not_38_out, not_39_out, not_40_out, not_41_out;

  not not_1 (not_1_out, E3);
  and and_1 (and_1_out, not_1_out, not_2_out);
  not not_2 (not_2_out, E0);
  not not_3 (not_3_out, E2);
  and and_2 (and_2_out, not_3_out, not_4_out);
  not not_4 (not_4_out, E1);
  not not_5 (not_5_out, E3);
  and and_3 (and_3_out, not_5_out, E2);
  and and_4 (and_4_out, E2, not_6_out);
  not not_6 (not_6_out, E0);
  not not_7 (not_7_out, E2);
  and and_5 (and_5_out, not_7_out, not_8_out);
  not not_8 (not_8_out, E1);
  not not_9 (not_9_out, E3);
  and and_6 (and_6_out, not_9_out, E1);
  not not_10 (not_10_out, E2);
  and and_7 (and_7_out, not_10_out, not_11_out);
  not not_11 (not_11_out, E0);
  not not_12 (not_12_out, E3);
  and and_8 (and_8_out, not_12_out, E1);
  not not_13 (not_13_out, E3);
  and and_9 (and_9_out, not_13_out, E2);
  and and_10 (and_10_out, E3, not_14_out, not_15_out);
  not not_14 (not_14_out, E2);
  not not_15 (not_15_out, E1);
  not not_16 (not_16_out, E3);
  and and_11 (and_11_out, not_16_out, not_17_out);
  not not_17 (not_17_out, E1);
  not not_18 (not_18_out, E2);
  and and_12 (and_12_out, not_18_out, not_19_out);
  not not_19 (not_19_out, E0);
  not not_20 (not_20_out, E3);
  and and_13 (and_13_out, not_20_out, E2, E0);
  not not_21 (not_21_out, E2);
  and and_14 (and_14_out, E3, not_21_out, E1);
  not not_22 (not_22_out, E3);
  not not_23 (not_23_out, E2);
  and and_15 (and_15_out, not_22_out, not_23_out, not_24_out);
  not not_24 (not_24_out, E1);
  not not_25 (not_25_out, E2);
  and and_16 (and_16_out, not_25_out, not_26_out, E0);
  not not_26 (not_26_out, E1);
  not not_27 (not_27_out, E3);
  and and_17 (and_17_out, not_27_out, E2, E0);
  and and_18 (and_18_out, E3, E1, not_28_out);
  not not_28 (not_28_out, E0);
  and and_19 (and_19_out, E3, E2, not_29_out);
  not not_29 (not_29_out, E0);
  not not_30 (not_30_out, E1);
  and and_20 (and_20_out, not_30_out, not_31_out);
  not not_31 (not_31_out, E0);
  not not_32 (not_32_out, E3);
  and and_21 (and_21_out, not_32_out, E1, E0);
  not not_33 (not_33_out, E3);
  and and_22 (and_22_out, not_33_out, E2);
  and and_23 (and_23_out, E3, not_34_out, not_35_out);
  not not_34 (not_34_out, E2);
  not not_35 (not_35_out, E1);
  and and_24 (and_24_out, E3, not_36_out);
  not not_36 (not_36_out, E0);
  not not_37 (not_37_out, E3);
  and and_25 (and_25_out, not_37_out, E0);
  not not_38 (not_38_out, E2);
  and and_26 (and_26_out, not_38_out, E1);
  not not_39 (not_39_out, E3);
  and and_27 (and_27_out, not_39_out, E2, not_40_out);
  not not_40 (not_40_out, E1);
  and and_28 (and_28_out, E3, not_41_out);
  not not_41 (not_41_out, E2);
  and and_29 (and_29_out, E3, E1);
  or or_1 (A, and_1_out, and_2_out, and_3_out, and_4_out);
  or or_2 (B, and_5_out, and_6_out);
  or or_3 (C, and_7_out, and_8_out, and_9_out, and_10_out);
  or or_4 (D, and_11_out, and_12_out, and_13_out, and_14_out);
  or or_5 (E, and_15_out, and_16_out, and_17_out, and_18_out, and_19_out);
  or or_6 (F, and_20_out, and_21_out, and_22_out, and_23_out, and_24_out);
  or or_7 (G, and_25_out, and_26_out, and_27_out, and_28_out, and_29_out);
endmodule
